# Fritzing sketch PlantaInteligente (saved by Fritzing 0.9.3b)
breadboards: 1

parts:
  U1 = NodeMCU V1.0
  LED1 = RGB LED - (4 legs) [package="5 mm [THT]"]
  T1 = LM35 Temperature Sensor [package="TO92 [THT]"]
  J1 = Piezo Speaker

nets:
  N1: U1.D0, LED1.blue_cathode
  N2: U1.D1, LED1.common_anode
  N3: U1.D2, LED1.red_cathode
  N4: U1.D3, J1.pin2
  N5: U1.3V3, T1.+Vs
  GND: U1.GND, LED1.green_cathode, T1.GND, J1.pin1
  N6: U1.A0, T1.Vout

custom parts:
  NodeMCU V1.0: ESP8266 based NodeMCU
